// Logisim project base.circ as structural Verilog: 1 circuit, main circuit Teste
module Teste (
  input  in_1,
  input  in_2,
  input  in_3,
  input  in_4,
  input  in_5,
  input  in_6,
  input  in_7
);

  wire and_1_out, and_2_out, and_3_out, and_4_out, and_5_out, and_6_out, clock_1_out, j_k_ff_1_q, j_k_ff_2_q,
       j_k_ff_3_q, or_1_out, or_2_out, or_3_out, or_4_out;

  Clock clock_1 (.out(clock_1_out));
  or or_1 (or_1_out, ~j_k_ff_2_q, j_k_ff_3_q);  // OR_Gate
  or or_2 (or_2_out, j_k_ff_3_q, j_k_ff_1_q);
  or or_3 (or_3_out, ~j_k_ff_1_q, j_k_ff_2_q);  // OR_Gate
  or or_4 (or_4_out, j_k_ff_2_q, j_k_ff_1_q);
  J_K_Flip_Flop j_k_ff_1 (
    .J(or_1_out), .clk(clock_1_out), .K(1'b1), .Q(j_k_ff_1_q), .preset(and_1_out), .reset(and_2_out));  // open: Qn, en
  and and_1 (and_1_out, in_1, in_5);
  and and_2 (and_2_out, in_2, in_5);
  J_K_Flip_Flop j_k_ff_2 (
    .J(j_k_ff_3_q), .clk(clock_1_out), .K(or_2_out), .Q(j_k_ff_2_q), .preset(and_3_out), .reset(and_4_out));  // open: Qn, en
  and and_3 (and_3_out, in_3, in_5);
  and and_4 (and_4_out, in_4, in_5);
  J_K_Flip_Flop j_k_ff_3 (
    .J(or_3_out), .clk(clock_1_out), .K(or_4_out), .Q(j_k_ff_3_q), .preset(and_5_out), .reset(and_6_out));  // open: Qn, en
  and and_5 (and_5_out, in_5, in_6);
  and and_6 (and_6_out, in_5, in_7);

  // Notes on the sheet:
  //   C
  //   B
  //   A
endmodule
