// Logisim project base.circ as structural Verilog: 1 circuit, main circuit base_2
module base_2 (
  input  in_1,
  input  in_2,
  input  in_3,
  input  in_4,
  input  in_5,
  input  in_6,
  input  in_7
);

  wire and_1_out, and_2_out, and_3_out, and_4_out, and_5_out, and_6_out, clock_1_out, j_k_ff_1_q, j_k_ff_2_q;

  Clock clock_1 (.out(clock_1_out));
  J_K_Flip_Flop j_k_ff_1 (
    .J(1'b1), .clk(clock_1_out), .K(j_k_ff_2_q), .Q(j_k_ff_1_q), .preset(and_1_out), .reset(and_2_out));  // open: Qn, en
  and and_1 (and_1_out, in_1, in_5);
  and and_2 (and_2_out, in_2, in_5);
  and and_3 (and_3_out, in_3, in_5);
  J_K_Flip_Flop j_k_ff_2 (
    .J(1'b1), .clk(clock_1_out), .K(j_k_ff_1_q), .Q(j_k_ff_2_q), .preset(and_3_out), .reset(and_4_out));  // open: Qn, en
  and and_4 (and_4_out, in_4, in_5);
  and and_5 (and_5_out, in_5, in_6);
  J_K_Flip_Flop j_k_ff_3 (
    .J(j_k_ff_1_q), .clk(clock_1_out), .K(j_k_ff_1_q), .preset(and_5_out), .reset(and_6_out));  // open: Q, Qn, en
  and and_6 (and_6_out, in_5, in_7);

  // Notes on the sheet:
  //   C
  //   B
  //   A
endmodule
