// Logisim project base.circ as structural Verilog: 1 circuit, main circuit base_2
module base_2 (
  input  X,
  input  Y
);

  wire and_1_out, and_2_out, and_3_out, and_4_out, and_5_out, and_6_out, and_7_out, and_8_out, and_9_out,
       clock_1_out, j_k_ff_1_q, j_k_ff_2_q, or_1_out, or_2_out, or_3_out, or_4_out;

  Clock clock_1 (.out(clock_1_out));
  and and_1 (and_1_out, ~X, ~Y, j_k_ff_2_q);  // AND_Gate
  and and_2 (and_2_out, Y, ~j_k_ff_2_q);  // AND_Gate
  and and_3 (and_3_out, X, ~j_k_ff_2_q);  // AND_Gate
  and and_4 (and_4_out, X, Y);
  and and_5 (and_5_out, ~X, j_k_ff_2_q);  // AND_Gate
  and and_6 (and_6_out, Y, j_k_ff_2_q);
  and and_7 (and_7_out, X, ~j_k_ff_2_q);  // AND_Gate
  or or_1 (or_1_out, ~Y, j_k_ff_1_q);  // OR_Gate
  and and_8 (and_8_out, ~X, ~j_k_ff_1_q);  // AND_Gate
  and and_9 (and_9_out, X, j_k_ff_1_q);
  or or_2 (or_2_out, and_1_out, and_2_out, and_3_out, and_4_out);
  or or_3 (or_3_out, and_5_out, and_6_out, and_7_out);
  or or_4 (or_4_out, and_8_out, ~Y, and_9_out);  // OR_Gate
  J_K_Flip_Flop j_k_ff_1 (
    .J(or_2_out), .clk(clock_1_out), .K(or_3_out), .Q(j_k_ff_1_q));  // open: Qn, preset, en, reset
  J_K_Flip_Flop j_k_ff_2 (
    .J(or_1_out), .clk(clock_1_out), .K(or_4_out), .Q(j_k_ff_2_q));  // open: Qn, preset, en, reset

  // Notes on the sheet:
  //   B
  //   A
endmodule
